// Logisim project Practica2.circ as structural Verilog: 1 circuit, main circuit main
// i
module main (
  input  A,
  input  B,
  input  A_2,
  input  A_3,
  input  B_2,
  input  nA,
  input  B_3,
  input  A_4,
  input  nB,
  input  nA_2,
  input  B_4,
  input  x3,
  input  x2,
  input  x1,
  input  x0,
  input  x2_2,
  input  x1_2,
  input  x0_2,
  input  x2_3,
  input  x1_3,
  input  x0_3,
  output A___B,
  output nA_3,
  output A___B_2,
  output nA___B,
  output A___nB_____nA___B,
  output F,
  output F1,
  output F2,
  output F3,
  output F1_2,
  output F2_2,
  output F3_2
);

  wire and_2_out, and_3_out, and_4_out, and_5_out, and_6_out, and_7_out, and_8_out, and_9_out, and_10_out,
       and_11_out, and_12_out, and_13_out, and_14_out, and_15_out, and_16_out, and_17_out, and_18_out,
       and_19_out, not_1_out, not_2_out, not_3_out, not_4_out, not_5_out, not_6_out, not_7_out, not_8_out,
       not_9_out, not_10_out, not_11_out, not_12_out, not_13_out, not_14_out, not_15_out, not_16_out,
       not_17_out, not_18_out, not_19_out, not_20_out, not_21_out, or_3_out;

  not not_1 (not_1_out, x3);
  not not_2 (not_2_out, x2);
  not not_3 (not_3_out, x1);
  Transistor transistor_1 (.in(1'b1), .out(nA_3), .gate(A_2));
  Transistor #(.\type ("n")) transistor_2 (.in(1'b0), .out(nA_3), .gate(A_2));
  not not_4 (not_4_out, nA);
  not not_5 (not_5_out, nB);
  not not_6 (not_6_out, nA_2);
  not not_7 (not_7_out, x2_2);
  not not_8 (not_8_out, x2_2);
  not not_9 (not_9_out, x1_2);
  not not_10 (not_10_out, x1_2);
  not not_11 (not_11_out, x0_2);
  not not_12 (not_12_out, x2_3);
  not not_13 (not_13_out, x1_3);
  not not_14 (not_14_out, x2_3);
  not not_15 (not_15_out, x0_3);
  not not_16 (not_16_out, x1_3);
  not not_17 (not_17_out, x0_3);
  not not_18 (not_18_out, x2_3);
  not not_19 (not_19_out, x1_3);
  not not_20 (not_20_out, x0_3);
  and and_1 (F3_2, x2_3, x1_3, x0_3);
  Transistor transistor_3 (.in(A), .out(A___B), .gate(A));
  Transistor #(.\type ("n")) transistor_4 (.in(B), .out(A___B), .gate(A));
  Transistor #(.\type ("n")) transistor_5 (.in(A_3), .out(A___B_2), .gate(A_3));
  Transistor transistor_6 (.in(B_2), .out(A___B_2), .gate(A_3));
  and and_2 (and_2_out, A_4, not_5_out);
  and and_3 (and_3_out, not_6_out, B_4);
  and and_4 (and_4_out, not_7_out, x0_2);
  and and_5 (and_5_out, not_8_out, x1_2);
  and and_6 (and_6_out, x2_2, not_9_out);
  not not_21 (not_21_out, x0_2);
  and and_7 (and_7_out, not_10_out, x0_2);
  and and_8 (and_8_out, x1_2, not_11_out);
  and and_9 (and_9_out, not_12_out, not_13_out, x0_3);
  and and_10 (and_10_out, not_14_out, x1_3, not_15_out);
  and and_11 (and_11_out, x2_3, not_16_out, not_17_out);
  and and_12 (and_12_out, not_18_out, x1_3, x0_3);
  and and_13 (and_13_out, x2_3, not_19_out, x0_3);
  and and_14 (and_14_out, x2_3, x1_3, not_20_out);
  or or_1 (nA___B, not_4_out, B_3);
  or or_2 (A___nB_____nA___B, and_2_out, and_3_out);
  and and_15 (and_15_out, x2, not_3_out, x0);
  and and_16 (and_16_out, not_2_out, x1, x0);
  and and_17 (and_17_out, not_1_out, x2, x0);
  and and_18 (and_18_out, not_1_out, not_2_out, x1);
  or or_3 (or_3_out, and_4_out, and_5_out);
  and and_19 (and_19_out, and_6_out, not_21_out);
  or or_4 (F2, and_7_out, and_8_out);
  or or_5 (F1_2, and_9_out, and_10_out, and_11_out);
  or or_6 (F2_2, and_12_out, and_13_out, and_14_out);
  or or_7 (F1, or_3_out, and_19_out);
  or or_8 (F, and_15_out, and_16_out, and_17_out, and_18_out);

  assign F3 = x0_2;

  // Notes on the sheet:
  //   Ejercicio 1a
  //   Ejercicio 1b
  //   Ejercicio 2a
  //   Ejercicio 2b
  //   Compuertas básicas
  //   Ejercicio 2c
  //   compuesta &&
  //   compuerta not
  //   compuerta or
endmodule
